# Fritzing sketch diagram (saved by Fritzing 0.9.3b)
breadboards: 2

parts:
  R1 = Resistor [tolerance=±10% resistance=1k package=THT]
  R2 = Resistor [tolerance=±5% resistance=1k package=THT]
  U1 = 74HC595 [package="DIP16 [THT]"]
  U2 = attiny85 [package=dip]  # not connected
  JP1 = USB_MICROB_PLUG [package=micro-b-th]  # not connected
  R3 = Resistor [tolerance=±5% resistance=1k package=THT]
  R4 = Resistor [tolerance=±5% resistance=1k package=THT]
  R5 = Resistor [tolerance=±5% resistance=1k package=THT]
  R6 = Resistor [tolerance=±5% resistance=1k package=THT]
  R7 = Resistor [tolerance=±5% resistance=1k package=THT]
  R8 = Resistor [tolerance=±5% resistance=1k package=THT]
  LED17 = LED - 3mm [color="Red (633nm)" package="3 mm [THT]"]
  LED18 = LED - 3mm [color="Red (633nm)" package="3 mm [THT]"]
  LED19 = LED - 3mm [color="Red (633nm)" package="3 mm [THT]"]
  LED20 = LED - 3mm [color="Red (633nm)" package="3 mm [THT]"]
  LED21 = LED - 3mm [color="Red (633nm)" package="3 mm [THT]"]
  LED22 = LED - 3mm [color="Red (633nm)" package="3 mm [THT]"]
  LED23 = LED - 3mm [color="Red (633nm)" package="3 mm [THT]"]
  LED24 = LED - 3mm [color="Red (633nm)" package="3 mm [THT]"]

nets:
  N1: R1.Pin_0, LED24.anode
  N2: R1.Pin_1, U1.Q0
  N3: R2.Pin_0, LED23.anode
  N4: R2.Pin_1, U1.Q1
  N5: U1.Q2, R3.Pin_1
  N6: U1.Q3, R4.Pin_1
  N7: U1.Q4, R5.Pin_1
  N8: U1.Q5, R6.Pin_1
  N9: U1.Q6, R7.Pin_1
  N10: U1.Q7, R8.Pin_1
  N11: U1.GND, U1.OE, LED17.cathode, LED18.cathode, LED19.cathode, LED20.cathode, LED21.cathode, LED22.cathode, LED23.cathode, LED24.cathode
  N12: U1.MR, U1.VCC
  N13: R3.Pin_0, LED22.anode
  N14: R4.Pin_0, LED21.anode
  N15: R5.Pin_0, LED20.anode
  N16: R6.Pin_0, LED19.anode
  N17: R7.Pin_0, LED18.anode
  N18: R8.Pin_0, LED17.anode
